// Logisim project template_alu.circ as structural Verilog: 5 circuits, main circuit alu
module alu (
  input  a,
  input  b,
  input  [1:0] opcode,
  input  CLK,
  output [7:0] c
);

  // Probe on c
endmodule

module sipo_8 (
  input  x,
  input  CLK,
  output [7:0] y
);
endmodule

module opcode_decoder (
  input  [1:0] opcode,
  output add_sub,
  output sub,
  output shift,
  output left
);
endmodule

module add_sub (
  input  [7:0] a,
  input  [7:0] b,
  input  sub,
  output [7:0] c
);

  // Probe on a
  // Probe on b
  // Probe on c
endmodule

module shifter (
  input  [7:0] x,
  input  left,
  output [7:0] y
);

  // Probe on x
  // Probe on y
endmodule
