// Logisim project template_graycode_208119883.circ as structural Verilog: 4 circuits, main circuit g2b1
module g2b1 (
  input  g,
  output b
);


  assign b = g;
endmodule

module g2b2 (
  input  [1:0] g,
  output [1:0] b
);

  wire g1, not_1_out;

  g2b1 g2b1_1 (.g(g[0]), .b(g1));
  not not_1 (not_1_out, g1);
  Multiplexer #(.enable("false")) multiplexer_1 (.in0(g1), .in1(not_1_out), .out(b[0]), .sel(g[1]));

  assign b[1] = g[1];
endmodule

module g2b3 (
  input  [2:0] g,
  output [2:0] b
);

  wire [1:0] g2, not_1_out;

  g2b2 g2b2_1 (.g(g[1:0]), .b(g2));
  not not_1 (not_1_out[0], g2[0]);
  not not_2 (not_1_out[1], g2[1]);
  Multiplexer #(.width(2), .enable("false")) multiplexer_1 (.in0(g2), .in1(not_1_out), .out(b[1:0]), .sel(g[2]));

  assign b[2] = g[2];
endmodule

module g2b4 (
  input  [3:0] g,
  output [3:0] b
);

  wire [2:0] g3, not_1_out;

  g2b3 g2b3_1 (.g(g[2:0]), .b(g3));
  not not_1 (not_1_out[0], g3[0]);
  not not_2 (not_1_out[1], g3[1]);
  not not_3 (not_1_out[2], g3[2]);
  Multiplexer #(.width(3), .enable("false")) multiplexer_1 (.in0(g3), .in1(not_1_out), .out(b[2:0]), .sel(g[3]));

  assign b[3] = g[3];
endmodule
