// Logisim project template_introduction.circ as structural Verilog: 7 circuits, main circuit 3_bit_carry
module _3_bit_carry (
  input  x,
  input  y,
  input  z,
  output c
);
endmodule

module parity (
  input  x,
  input  y,
  output z
);
endmodule

module equivalence (
  input  x,
  input  y,
  output z
);
endmodule

module tautology (
  input  x,
  input  y,
  output z
);
endmodule

module ztor (
  input  [5:0] x,
  output y
);
endmodule

module ztand (
  input  [5:0] x,
  output y
);
endmodule

module pf4 (
  input  [3:0] x,
  output [3:0] y
);
endmodule
